// Logisim project add.circ as structural Verilog
module \_1位加法  (
  input  in_1,
  input  a,
  input  b,
  output f,
  output cout
);

  wire and_1_out, and_2_out, and_3_out, xor_1_out;

  xor xor_1 (xor_1_out, a, b);
  xor xor_2 (f, in_1, xor_1_out);
  and and_1 (and_1_out, in_1, a);
  and and_2 (and_2_out, in_1, b);
  and and_3 (and_3_out, a, b);
  or or_1 (cout, and_1_out, and_2_out, and_3_out);

  // Notes on the sheet:
  //   in_1: pull=down
endmodule

module \_4位加法  (
  input  [3:0] in_1,
  input  in_2,
  input  [3:0] in_3,
  output [3:0] out_4,
  output out_5
);

  wire \n1位加法_1_cout , \n1位加法_2_cout , \n1位加法_3_cout ;

  \_1位加法  \u_1位加法_1  (.a(in_1[0]), .b(in_3[0]), .in_1(in_2), .f(out_4[0]), .cout(\n1位加法_1_cout ));
  \_1位加法  \u_1位加法_2  (.a(in_1[1]), .b(in_3[1]), .in_1(\n1位加法_1_cout ), .f(out_4[1]), .cout(\n1位加法_2_cout ));
  \_1位加法  \u_1位加法_3  (.a(in_1[2]), .b(in_3[2]), .in_1(\n1位加法_2_cout ), .f(out_4[2]), .cout(\n1位加法_3_cout ));
  \_1位加法  \u_1位加法_4  (.a(in_1[3]), .b(in_3[3]), .in_1(\n1位加法_3_cout ), .f(out_4[3]), .cout(out_5));

  // Notes on the sheet:
  //   in_2: pull=down
endmodule

module \_8位加法  (
  input  in_1,
  input  [7:0] a,
  input  [7:0] b,
  output [7:0] sum,
  output cout
);

  wire \n4位加法_1_out_5 ;

  \_4位加法  \u_4位加法_1  (.out_4(sum[3:0]), .out_5(\n4位加法_1_out_5 ), .in_1(a[3:0]), .in_3(b[3:0]), .in_2(in_1));
  \_4位加法  \u_4位加法_2  (.out_4(sum[7:4]), .out_5(cout), .in_1(a[7:4]), .in_3(b[7:4]), .in_2(\n4位加法_1_out_5 ));

  // Notes on the sheet:
  //   in_1: pull=down
endmodule

module \_32位加法  (
  input  in_1,
  input  [31:0] in_2,
  input  [31:0] in_3,
  output [31:0] out_4,
  output out_5
);

  wire \n8位加法_1_cout , \n8位加法_2_cout , \n8位加法_3_cout ;

  // Probe on in_2
  // Probe on in_3
  \_8位加法  \u_8位加法_1  (.a(in_2[7:0]), .b(in_3[7:0]), .in_1(in_1), .sum(out_4[7:0]), .cout(\n8位加法_1_cout ));
  \_8位加法  \u_8位加法_2  (.a(in_2[15:8]), .b(in_3[15:8]), .in_1(\n8位加法_1_cout ), .sum(out_4[15:8]), .cout(\n8位加法_2_cout ));
  \_8位加法  \u_8位加法_3  (
    .a(in_2[23:16]), .b(in_3[23:16]), .in_1(\n8位加法_2_cout ), .sum(out_4[23:16]), .cout(\n8位加法_3_cout ));
  \_8位加法  \u_8位加法_4  (.a(in_2[31:24]), .b(in_3[31:24]), .in_1(\n8位加法_3_cout ), .sum(out_4[31:24]), .cout(out_5));
  // Probe on out_4

  // Notes on the sheet:
  //   in_3: pull=down
  //   in_2: pull=down
  //   in_1: pull=down
endmodule

module \补码  (
  input  in_1,
  input  [31:0] in_2,
  output [31:0] out_3
);

  wire [31:0] not_1_out;

  assign not_1_out = ~in_2;  // NOT_Gate not_1, 32 bits wide
  \_32位加法  \u_32位加法_1  (.in_2(not_1_out), .out_4(out_3), .in_1(in_1));  // open: in_3, out_5

  // Notes on the sheet:
  //   in_1: pull=up
endmodule

module \_32位加减法  (
  input  [31:0] a,
  input  [31:0] b,
  input  sub,
  output [31:0] sum,
  output cout,
  output OF
);

  wire [31:0] multiplexer_1_out, \补码_1_out_3 ;

  // Probe on a
  // Probe on b
  \补码  \u_补码_1  (.in_2(b), .out_3(\补码_1_out_3 ));  // open: in_1
  Multiplexer #(.width(32), .enable("false")) multiplexer_1 (
    .in0(b), .in1(\补码_1_out_3 ), .out(multiplexer_1_out), .sel(sub));
  \_32位加法  \u_32位加法_1  (.in_2(a), .in_3(multiplexer_1_out), .out_4(sum), .out_5(cout));  // open: in_1
  // Probe on multiplexer_1_out
  // Probe on sum
  xor xor_1 (OF, cout, sub);
endmodule

module \二路选择器  (
  input  in_1,
  input  in_2,
  input  in_3,
  output out_4
);

  wire and_1_out, and_2_out;

  and and_1 (and_1_out, in_1, ~in_3);  // AND_Gate
  and and_2 (and_2_out, in_3, in_2);
  or or_1 (out_4, and_1_out, and_2_out);
endmodule

module \两端口二路选择器器  (
  input  [1:0] in_1,
  input  [1:0] in_2,
  input  in_3,
  output [1:0] out_4
);

  \二路选择器  \u_二路选择器_1  (.in_1(in_1[0]), .in_2(in_1[0]), .in_3(in_3), .out_4(out_4[0]));
  \二路选择器  \u_二路选择器_2  (.in_1(in_1[1]), .in_2(in_2[1]), .in_3(in_3), .out_4(out_4[1]));

  assign in_2[0] = in_1[0];
endmodule
